# Fritzing sketch rangkaian (saved by Fritzing 0.9.2b)
breadboards: 1

parts:
  Part1 = Arduino Uno (Rev3)
  7_Segment1 = 7 Segment Display
  7_Segment2 = 7 Segment Display  # not connected
  7_Segment3 = 7 Segment Display  # not connected
  7_Segment4 = 7 Segment Display
  K1 = Relay [part_number=FRS1B-S package=THT]
  S1 = Pushbutton [package=THT]
  J1 = Piezo Speaker
  IC1 = IC, DIP package, 14 pins [chip_label=74LS164]
  R1 = Resistor [tolerance=±5% resistance=220 package=THT]  # not connected
  R2 = Resistor [tolerance=±5% resistance=220 package=THT]  # not connected
  R3 = Resistor [tolerance=±5% resistance=220 package=THT]  # not connected
  R5 = Resistor [tolerance=±5% resistance=220 package=THT]  # not connected
  LED1 = LED - 5mm [color="Blue (470nm)" package="5 mm [THT]"]
  IC2 = IC, DIP package, 8 pins [chip_label=ACS712]
  Power_plug1 = Power plug
  Fuse1 = Fuse with Handler [part_number=Htc-15m]
  Power_plug2 = Power plug
  LED2 = LED - 5mm [color="Red (633nm)" package="5 mm [THT]"]

nets:
  N1: Part1.A0, IC2.pin7
  N2: Part1.D8, IC1.pin1
  N3: Part1.D9_PWM, IC1.pin9
  N4: Part1.D10_PWM/SS, K1.COIL2
  N5: Part1.D11_PWM/MOSI, J1.pin2, LED2.anode
  N6: Part1.D13/SCK, LED1.anode
  N7: Part1.D2, S1.leg0
  N8: Part1.D4, Part1.D5_PWM, Part1.D6_PWM, Part1.D7
  N9: Part1.5V, IC1.pin2, IC1.pin8, IC1.pin14, IC2.pin8
  N10: Part1.GND, K1.COIL1, S1.leg1, J1.pin1, IC1.pin7, LED1.cathode, IC2.pin5, LED2.cathode
  N11: 7_Segment1.Segment_G, IC1.pin13
  N12: 7_Segment1.Segment_F, IC1.pin12
  N13: 7_Segment1.common_anode, IC1.pin11
  N14: 7_Segment1.Segment_E, IC1.pin10
  N15: 7_Segment4.common_anode, IC1.pin5
  N16: 7_Segment4.Segment_C, IC1.pin6
  N17: 7_Segment4.Segment_B, IC1.pin4
  N18: 7_Segment4.Segment_A, IC1.pin3
  N19: K1.A, IC2.pin3, IC2.pin4
  N20: K1.B, Fuse1.Connector1
  N21: IC2.pin1, IC2.pin2
  GND: Power_plug1.GND, Power_plug2.GND
  N22: Power_plug1.VCC, Fuse1.Connector2
